# Fritzing sketch Pendant (saved by Fritzing 0.8.7b)
circuit board: 4.9882cm x 3.25775cm
breadboards: 1

parts:
  Pad1 = Pad [width=2.35185185185185 height=2.25777777777778 connect=center]
  Pad2 = Pad [width=2.35185185185185 height=2.25777777777778 connect=center]
  R3 = Resistor [tolerance=±5% resistance=220 package="0805 [SMD]"]
  R4 = Resistor [tolerance=±5% resistance=220 package="0805 [SMD]"]
  R5 = Resistor [tolerance=±5% resistance=220 package="0805 [SMD]"]
  R6 = Resistor [tolerance=±5% resistance=220 package="0805 [SMD]"]
  R7 = Resistor [tolerance=±5% resistance=220 package="0805 [SMD]"]
  LED1 = smd LED [color="Red (633nm)" package="1206 [SMD]"]
  LED2 = smd LED [color="Red (633nm)" package="1206 [SMD]"]
  LED3 = smd LED [color="Red (633nm)" package="1206 [SMD]"]
  LED4 = smd LED [color="Red (633nm)" package="1206 [SMD]"]
  LED5 = smd LED [color="Red (633nm)" package="1206 [SMD]"]
  LED6 = smd LED [color="Red (633nm)" package="1206 [SMD]"]
  LED7 = smd LED [color="Red (633nm)" package="1206 [SMD]"]
  LED8 = smd LED [color="Red (633nm)" package="1206 [SMD]"]
  LED9 = smd LED [color="Red (633nm)" package="1206 [SMD]"]
  LED10 = smd LED [color="Red (633nm)" package="1206 [SMD]"]
  LED14 = smd LED [color="Red (633nm)" package="1206 [SMD]"]
  LED17 = smd LED [color="Red (633nm)" package="1206 [SMD]"]
  LED16 = smd LED [color="Red (633nm)" package="1206 [SMD]"]
  LED13 = smd LED [color="Red (633nm)" package="1206 [SMD]"]
  LED18 = smd LED [color="Red (633nm)" package="1206 [SMD]"]
  LED20 = smd LED [color="Red (633nm)" package="1206 [SMD]"]
  LED15 = smd LED [color="Red (633nm)" package="1206 [SMD]"]
  LED12 = smd LED [color="Red (633nm)" package="1206 [SMD]"]
  LED11 = smd LED [color="Red (633nm)" package="1206 [SMD]"]
  LED19 = smd LED [color="Red (633nm)" package="1206 [SMD]"]
  Pad3 = Pad [width=2 height=0.5 connect=center]
  Pad4 = Pad [width=2 height=0.5 connect=center]
  Pad5 = Pad [width=2 height=0.5 connect=center]
  Pad6 = Pad [width=2 height=0.5 connect=center]
  Pad7 = Pad [width=2 height=0.5 connect=center]
  Pad8 = Pad [width=2 height=0.5 connect=center]
  Pad9 = Pad [width=2 height=0.5 connect=center]
  Pad10 = Pad [width=2 height=0.5 connect=center]
  Pad11 = Pad [width=2.35185185185185 height=2.25777777777778 connect=center]
  Pad12 = Pad [width=2.35185185185185 height=2.25777777777778 connect=center]
  Pad13 = Pad [width=2.35185185185185 height=2.25777777777778 connect=center]
  Pad14 = Pad [width=2.35185185185185 height=2.25777777777778 connect=center]
  Pad15 = Pad [width=2.35185185185185 height=2.25777777777778 connect=center]
  Pad16 = Pad [width=2.35185185185185 height=2.25777777777778 connect=center]

nets:
  N1: Pad1.pad, Pad7.pad
  N2: Pad2.pad, Pad3.pad
  N3: R3.Pin_0, Pad6.pad, Pad12.pad
  N4: R3.Pin_1, LED1.cathode, LED2.anode, LED9.cathode, LED10.anode, LED16.cathode, LED20.cathode, LED15.anode, LED19.anode
  N5: R4.Pin_0, LED7.anode, LED8.cathode, LED14.anode, LED17.cathode, LED13.cathode, LED18.anode, LED20.anode, LED19.cathode
  N6: R4.Pin_1, Pad8.pad, Pad15.pad
  N7: R5.Pin_0, LED5.anode, LED6.cathode, LED7.cathode, LED8.anode, LED16.anode, LED15.cathode, LED12.anode, LED11.cathode
  N8: R5.Pin_1, Pad9.pad, Pad13.pad
  N9: R6.Pin_0, Pad5.pad, Pad11.pad
  N10: R6.Pin_1, LED1.anode, LED2.cathode, LED3.cathode, LED4.anode, LED17.anode, LED18.cathode, LED12.cathode, LED11.anode
  N11: R7.Pin_0, Pad4.pad, Pad16.pad
  N12: R7.Pin_1, LED3.anode, LED4.cathode, LED5.cathode, LED6.anode, LED9.anode, LED10.cathode, LED14.cathode, LED13.anode
  N13: Pad10.pad, Pad14.pad

notes:
  +
  -
